# Fritzing sketch house Sketch (saved by Fritzing 0.9.2b)
breadboards: 1

parts:
  Componente1 = Arduino Yun
  LED15 = smd LED [color="Red (633nm)" package="0603 [SMD]"]
  R1 = Resistor [tolerance=±5% resistance=220 package=THT]
  LED16 = smd LED [color="Red (633nm)" package="0603 [SMD]"]
  LED17 = smd LED [color="Red (633nm)" package="0603 [SMD]"]
  R2 = Resistor [tolerance=±5% resistance=220 package=THT]
  R3 = Resistor [tolerance=±5% resistance=220 package=THT]
  R4 = Resistor [tolerance=±5% resistance=220 package=THT]
  R5 = Resistor [tolerance=±5% resistance=220 package=THT]
  R6 = Resistor [tolerance=±5% resistance=220 package=THT]
  R7 = Resistor [tolerance=±5% resistance=220 package=THT]
  R8 = Resistor [tolerance=±5% resistance=220 package=THT]
  R9 = Resistor [tolerance=±5% resistance=220 package=THT]
  R10 = Resistor [tolerance=±5% resistance=220 package=THT]
  R11 = Resistor [tolerance=±5% resistance=220 package=THT]
  LED18 = smd LED [color="Red (633nm)" package="0603 [SMD]"]
  LED19 = smd LED [color="Red (633nm)" package="0603 [SMD]"]
  LED20 = smd LED [color="Red (633nm)" package="0603 [SMD]"]
  LED21 = smd LED [color="Red (633nm)" package="0603 [SMD]"]
  LED22 = smd LED [color="Red (633nm)" package="0603 [SMD]"]
  LED23 = smd LED [color="Red (633nm)" package="0603 [SMD]"]
  LED24 = smd LED [color="Red (633nm)" package="0603 [SMD]"]
  LED25 = smd LED [color="Red (633nm)" package="0603 [SMD]"]
  LED26 = smd LED [color="Red (633nm)" package="0603 [SMD]"]
  LED27 = smd LED [color="Red (633nm)" package="0603 [SMD]"]
  LED28 = smd LED [color="Red (633nm)" package="0603 [SMD]"]
  LED29 = smd LED [color="Red (633nm)" package="0603 [SMD]"]
  R12 = Resistor [tolerance=±5% resistance=220 package=THT]
  R13 = Resistor [tolerance=±5% resistance=220 package=THT]
  R14 = Resistor [tolerance=±5% resistance=220 package=THT]
  R15 = Resistor [tolerance=±5% resistance=220 package=THT]

nets:
  N1: Componente1.A0, R1.Pin_0
  N2: Componente1.A1, R2.Pin_0
  N3: Componente1.A2, R3.Pin_0
  N4: Componente1.D8, R10.Pin_0
  N5: Componente1.D9_PWM, R11.Pin_0
  N6: Componente1.D10_PWM/SS, R12.Pin_0
  N7: Componente1.D11_PWM/MOSI, R13.Pin_0
  N8: Componente1.D12/MISO, R14.Pin_0
  N9: Componente1.D13/SCK, R15.Pin_0
  N10: Componente1.GND, LED15.cathode, LED16.cathode, LED17.cathode, LED18.cathode, LED19.cathode, LED20.cathode, LED21.cathode, LED22.cathode, LED23.cathode, LED24.cathode, LED25.cathode, LED26.cathode, LED27.cathode, LED28.cathode, LED29.cathode
  N11: Componente1.D2/SDA, Componente1.D2, R4.Pin_0
  N12: Componente1.D3/SCL, Componente1.D3_PWM, R5.Pin_0
  N13: Componente1.D4, R6.Pin_0
  N14: Componente1.D5_PWM, R7.Pin_0
  N15: Componente1.D6_PWM, R8.Pin_0
  N16: Componente1.D7, R9.Pin_0
  N17: LED15.anode, R1.Pin_1
  N18: LED16.anode, R2.Pin_1
  N19: LED17.anode, R3.Pin_1
  N20: R4.Pin_1, LED18.anode
  N21: R5.Pin_1, LED19.anode
  N22: R6.Pin_1, LED20.anode
  N23: R7.Pin_1, LED21.anode
  N24: R8.Pin_1, LED22.anode
  N25: R9.Pin_1, LED23.anode
  N26: R10.Pin_1, LED24.anode
  N27: R11.Pin_1, LED25.anode
  N28: LED26.anode, R12.Pin_1
  N29: LED27.anode, R13.Pin_1
  N30: LED28.anode, R14.Pin_1
  N31: LED29.anode, R15.Pin_1

// code stored in the sketch: switch.ino

/*


 to visit the html page, go in your browser and type:

 http://arduino.local/sd/switch

 where "arduino" is your board name, after uploading 	

 the sketch via WiFi.

 

 On the web page, there's a switch that triggers

 a TinkerKit! Relay and the LED 13 on the board

 

 10/13 - Matteo Loglio (matlo.me)

 */



#include <TinkerKit.h>

#include <Bridge.h>

#include <YunServer.h>

#include <YunClient.h>



// Listen on default port 5555, the webserver on the Yun

// will forward there all the HTTP requests for us.

YunServer server;



TKRelay relay(O0);



void setup() {

  Serial.begin(9600);



  // Bridge startup

  pinMode(13,OUTPUT);
  pinMode(12,OUTPUT); //extra
  pinMode(11,OUTPUT); //extra
  pinMode(10,OUTPUT); //extra
  pinMode(9,OUTPUT); 	//extra
  pinMode(8,OUTPUT); 	//extra
  pinMode(7,OUTPUT); 	//extra
  pinMode(6,OUTPUT); 	//extra
  pinMode(5,OUTPUT); 	//extra
  pinMode(4,OUTPUT); 	//extra
  pinMode(3,OUTPUT); 	//extra
  pinMode(2,OUTPUT); 	//extra
  pinMode(A0,OUTPUT); //extra
  pinMode(A1,OUTPUT); //extra
  pinMode(A2,OUTPUT); //extra

  Bridge.begin();



  // Listen for incoming connection only from localhost

  // (no one from the external network could connect)

  server.listenOnLocalhost();

  server.begin();

}



void loop() {

  // Get clients coming from server

  YunClient client = server.accept();



  // There is a new client?

  if (client) {



    String command = client.readStringUntil('/');



    // is "relay" command?

    if (command == "relay") {



      int stat = client.parseInt();



      if (stat == 1) {

        digitalWrite(13, HIGH);

        relay.on();      

      } 

      else {

        digitalWrite(13, LOW);

        relay.off();

      }

    }



    // Close connection and free resources.

    client.stop();

  }



  delay(50); // Poll every 50ms

}
